// Logisim project 737215-BR32.circ as structural Verilog: 2 circuits, main circuit BR4
module BR4 (
  input  regW,
  input  CLK,
  input  Clear,
  input  [1:0] RA,
  input  [1:0] RW,
  input  [31:0] busW,
  input  [1:0] RB,
  output [31:0] busA,
  output [31:0] busB
);

  wire and_1_out, and_2_out, and_3_out, and_4_out, decoder_1_out0, decoder_1_out1, decoder_1_out2,
       decoder_1_out3;
  wire [31:0] register_1_q, register_2_q, register_3_q, register_4_q;

  Decoder #(.select(2), .enable("false")) decoder_1 (
    .out0(decoder_1_out0), .out1(decoder_1_out1), .out2(decoder_1_out2), .out3(decoder_1_out3), .sel(RW));
  and and_1 (and_1_out, regW, decoder_1_out0);
  and and_2 (and_2_out, regW, decoder_1_out1);
  and and_3 (and_3_out, regW, decoder_1_out2);
  and and_4 (and_4_out, regW, decoder_1_out3);
  Register #(.width(32)) register_1 (.D(busW), .en(and_1_out), .Q(register_1_q), .clk(CLK), .clr(Clear));
  Register #(.width(32)) register_2 (.D(busW), .en(and_2_out), .Q(register_2_q), .clk(CLK), .clr(Clear));
  Register #(.width(32)) register_3 (.D(busW), .en(and_3_out), .Q(register_3_q), .clk(CLK), .clr(Clear));
  Register #(.width(32)) register_4 (.D(busW), .en(and_4_out), .Q(register_4_q), .clk(CLK), .clr(Clear));
  Multiplexer #(.select(2), .width(32), .enable("false")) multiplexer_1 (
    .in0(register_1_q), .in1(register_2_q), .in2(register_3_q), .in3(register_4_q), .out(busA), .sel(RA));
  Multiplexer #(.select(2), .width(32), .enable("false")) multiplexer_2 (
    .in0(register_1_q), .in1(register_2_q), .in2(register_3_q), .in3(register_4_q), .out(busB), .sel(RB));
endmodule

module BR32 (
  input  [4:0] RA,
  input  clear,
  input  clk,
  input  regW,
  input  [4:0] RW,
  input  [31:0] busW,
  input  [4:0] RB,
  output [31:0] busA,
  output [31:0] busB
);

  wire regW0, regW1, regW2, regW3, regW4, regW5, regW6, regW7, s0, s1, s2, s3, s4, s5, s6, s7;
  wire [31:0] a0, a1, a2, a3, a4, a5, a6, a7, b0, b1, b2, b3, b4, b5, b6, b7;

  Decoder #(.select(3), .enable("false")) decoder_1 (
    .out0(s0), .out1(s1), .out2(s2), .out3(s3), .out4(s4), .out5(s5), .out6(s6), .out7(s7), .sel(RW[2:0]));
  and and_1 (regW0, regW, s0);
  and and_2 (regW1, regW, s1);
  and and_3 (regW2, regW, s2);
  and and_4 (regW3, regW, s3);
  and and_5 (regW4, regW, s4);
  and and_6 (regW5, regW, s5);
  and and_7 (regW6, regW, s6);
  and and_8 (regW7, regW, s7);
  BR4 br4_1 (
    .regW(regW0), .CLK(clk), .Clear(clear), .busA(a0), .RA(RA[4:3]), .busB(b0), .RW(RW[4:3]), .busW(busW),
    .RB(RB[4:3]));
  BR4 br4_2 (
    .regW(regW1), .CLK(clk), .Clear(clear), .busA(a1), .RA(RA[4:3]), .busB(b1), .RW(RW[4:3]), .busW(busW),
    .RB(RB[4:3]));
  BR4 br4_3 (
    .regW(regW2), .CLK(clk), .Clear(clear), .busA(a2), .RA(RA[4:3]), .busB(b2), .RW(RW[4:3]), .busW(busW),
    .RB(RB[4:3]));
  BR4 br4_4 (
    .regW(regW3), .CLK(clk), .Clear(clear), .busA(a3), .RA(RA[4:3]), .busB(b3), .RW(RW[4:3]), .busW(busW),
    .RB(RB[4:3]));
  BR4 br4_5 (
    .regW(regW4), .CLK(clk), .Clear(clear), .busA(a4), .RA(RA[4:3]), .busB(b4), .RW(RW[4:3]), .busW(busW),
    .RB(RB[4:3]));
  BR4 br4_6 (
    .regW(regW5), .CLK(clk), .Clear(clear), .busA(a5), .RA(RA[4:3]), .busB(b5), .RW(RW[4:3]), .busW(busW),
    .RB(RB[4:3]));
  BR4 br4_7 (
    .regW(regW6), .CLK(clk), .Clear(clear), .busA(a6), .RA(RA[4:3]), .busB(b6), .RW(RW[4:3]), .busW(busW),
    .RB(RB[4:3]));
  BR4 br4_8 (
    .regW(regW7), .CLK(clk), .Clear(clear), .busA(a7), .RA(RA[4:3]), .busB(b7), .RW(RW[4:3]), .busW(busW),
    .RB(RB[4:3]));
  Multiplexer #(.select(3), .width(32), .enable("false")) multiplexer_1 (
    .in0(a0), .in1(a1), .in2(a2), .in3(a3), .in4(a4), .in5(a5), .in6(a6), .in7(a7), .out(busA), .sel(RA[2:0]));
  Multiplexer #(.select(3), .width(32), .enable("false")) multiplexer_2 (
    .in0(b0), .in1(b1), .in2(b2), .in3(b3), .in4(b4), .in5(b5), .in6(b6), .in7(b7), .out(busB), .sel(RB[2:0]));

  // Other names for the same wires on the sheet: ent[31:0] = busW; RA_t[1:0] = RA[4:3]; RB_t[1:0] = RB[4:3];
  //   RW_t[1:0] = RW[4:3]
endmodule
