// Logisim project 737215-multi2.circ as structural Verilog: 3 circuits, main circuit PROC1
module BR4 (
  input  [1:0] RA,
  input  [1:0] RB,
  input  [1:0] RW,
  input  regW,
  input  clear,
  input  clk,
  input  [31:0] busW,
  output [31:0] busA,
  output [31:0] busB
);

  wire decod1, decod2, decod3, decod4;
  wire [31:0] sal1, sal2, sal3, sal4;

  Decoder #(.select(2), .disabled(0)) decoder_1 (
    .out0(decod1), .out1(decod2), .out2(decod3), .out3(decod4), .sel(RW), .en(regW));
  Register #(.width(32)) register_1 (.D(busW), .en(decod1), .Q(sal1), .clk(clk), .clr(clear));
  Register #(.width(32)) register_2 (.D(busW), .en(decod2), .Q(sal2), .clk(clk), .clr(clear));
  Register #(.width(32)) register_3 (.D(busW), .en(decod3), .Q(sal3), .clk(clk), .clr(clear));
  Register #(.width(32)) register_4 (.D(busW), .en(decod4), .Q(sal4), .clk(clk), .clr(clear));
  Multiplexer #(.select(2), .width(32)) multiplexer_1 (
    .in0(sal1), .in1(sal2), .in2(sal3), .in3(sal4), .out(busA), .sel(RA));  // open: en
  Multiplexer #(.select(2), .width(32)) multiplexer_2 (
    .in0(sal1), .in1(sal2), .in2(sal3), .in3(sal4), .out(busB), .sel(RB));  // open: en
endmodule

module BR32 (
  input  [4:0] RA,
  input  [4:0] RB,
  input  [4:0] RW,
  input  [31:0] busW,
  input  regW,
  input  clk,
  input  clear,
  output [31:0] busA,
  output [31:0] busB
);

  wire Decod1, Decod2, Decod3, Decod4, Decod5, Decod6, Decod7, Decod8;
  wire [31:0] busA1, busA2, busA3, busA4, busA5, busA6, busA7, busA8, busB1, busB2, busB3, busB4, busB5,
       busB6, busB7, busB8;

  Decoder #(.select(3), .disabled(0)) decoder_1 (
    .out0(Decod1), .out1(Decod2), .out2(Decod3), .out3(Decod4), .out4(Decod5), .out5(Decod6), .out6(Decod7),
    .out7(Decod8), .sel(RW[2:0]), .en(regW));
  BR4 br4_1 (
    .regW(Decod1), .RW(RW[4:3]), .busW(busW), .busA(busA1), .busB(busB1), .clear(clear), .clk(clk),
    .RA(RA[4:3]), .RB(RB[4:3]));
  BR4 br4_2 (
    .regW(Decod2), .RW(RW[4:3]), .busW(busW), .busA(busA2), .busB(busB2), .clear(clear), .clk(clk),
    .RA(RA[4:3]), .RB(RB[4:3]));
  BR4 br4_3 (
    .regW(Decod3), .RW(RW[4:3]), .busW(busW), .busA(busA3), .busB(busB3), .clear(clear), .clk(clk),
    .RA(RA[4:3]), .RB(RB[4:3]));
  BR4 br4_4 (
    .regW(Decod4), .RW(RW[4:3]), .busW(busW), .busA(busA4), .busB(busB4), .clear(clear), .clk(clk),
    .RA(RA[4:3]), .RB(RB[4:3]));
  BR4 br4_5 (
    .regW(Decod5), .RW(RW[4:3]), .busW(busW), .busA(busA5), .busB(busB5), .clear(clear), .clk(clk),
    .RA(RA[4:3]), .RB(RB[4:3]));
  BR4 br4_6 (
    .regW(Decod6), .RW(RW[4:3]), .busW(busW), .busA(busA6), .busB(busB6), .clear(clear), .clk(clk),
    .RA(RA[4:3]), .RB(RB[4:3]));
  BR4 br4_7 (
    .regW(Decod7), .RW(RW[4:3]), .busW(busW), .busA(busA7), .busB(busB7), .clear(clear), .clk(clk),
    .RA(RA[4:3]), .RB(RB[4:3]));
  BR4 br4_8 (
    .regW(Decod8), .RW(RW[4:3]), .busW(busW), .busA(busA8), .busB(busB8), .clear(clear), .clk(clk),
    .RA(RA[4:3]), .RB(RB[4:3]));
  Multiplexer #(.select(3), .width(32), .disabled(0)) multiplexer_1 (
    .in0(busA1), .in1(busA2), .in2(busA3), .in3(busA4), .in4(busA5), .in5(busA6), .in6(busA7), .in7(busA8),
    .out(busA), .sel(RA[2:0]));  // open: en
  Multiplexer #(.select(3), .width(32), .disabled(0)) multiplexer_2 (
    .in0(busB1), .in1(busB2), .in2(busB3), .in3(busB4), .in4(busB5), .in5(busB6), .in6(busB7), .in7(busB8),
    .out(busB), .sel(RB[2:0]));  // open: en

  // Other names for the same wires on the sheet: RAmux[2:0] = RA[2:0]; RAent[1:0] = RA[4:3]; RBmux[2:0] = RB[2:0];
  //   RBent[1:0] = RB[4:3]; RWdecod[2:0] = RW[2:0]; RWent[1:0] = RW[4:3]
endmodule

module PROC1 (
);

  wire and_1_out, clear, clk, comp, IRwr, memWr, mux, muxPC, not_1_out, pc, RA, RAMread, RB, RC, regW,
       tty_ctrl_1_clk2, tty_ctrl_1_clr, tty_ctrl_1_out;
  wire [1:0] mux2;
  wire [2:0] ent;
  wire [3:0] register_2_q, rom_2_data;
  wire [4:0] multiplexer_2_out;
  wire [6:0] entrada, tty_ctrl_1_dout;
  wire [12:0] IR_q;
  wire [15:0] adder_1_out, branch, multiplexer_1_out, register_1_q;
  wire [31:0] adder_2_out, bit_extender_1_out, br32_1_busa, br32_1_busb, multiplexer_3_out, rom_1_data,
       salMem, salRA, salRB, salRC;
  wire [31:7] ram_1_data;

  Adder #(.width(16)) adder_1 (.a(register_1_q), .b(16'h1), .out(adder_1_out));  // open: cin, cout
  Multiplexer #(.width(16), .enable("false")) multiplexer_1 (
    .in0(adder_1_out), .in1(branch), .out(multiplexer_1_out), .sel(and_1_out));
  and and_1 (and_1_out, comp, muxPC);
  Register #(.width(16)) register_1 (.D(multiplexer_1_out), .en(pc), .Q(register_1_q), .clk(clk), .clr(clear));
  tty_ctrl tty_ctrl_1 (
    .A({16{1'b1}}), .E(memWr), .out(tty_ctrl_1_out), .clr(tty_ctrl_1_clr), .D(entrada), .clk(clk),
    .Dout(tty_ctrl_1_dout), .clk2(tty_ctrl_1_clk2));
  TTY tty_1 (.data(tty_ctrl_1_dout), .clk(tty_ctrl_1_clk2), .we(tty_ctrl_1_out), .clr(tty_ctrl_1_clr));
  ROM #(.addrWidth(16), .dataWidth(32)) rom_1 (.addr(register_1_q), .data(rom_1_data));  // open: sel
  // Probe on ent
  Register #(.width(32)) IR (.D(rom_1_data), .en(IRwr), .Q({ent, branch, IR_q}), .clk(clk), .clr(clear));
  Clock clock_1 (.out(clk));
  Button button_1 (.out(clear));
  // Probe on {branch[1:0], IR_q[12:10]}
  assign bit_extender_1_out = {{16{1'b0}}, branch};  // Bit_Extender bit_extender_1
  Register #(.width(4)) register_2 (.D(rom_2_data), .en(1'b1), .Q(register_2_q), .clk(clk), .clr(clear));
  // Probe on IR_q[9:5]
  // Probe on IR_q[4:0]
  // Probe on branch
  // Probe on {register_2_q, ent}
  // Probe on multiplexer_2_out
  Multiplexer #(.width(5), .enable("false")) multiplexer_2 (
    .in0({branch[1:0], IR_q[12:10]}), .in1(IR_q[4:0]), .out(multiplexer_2_out), .sel(mux));
  Multiplexer #(.select(2), .width(32), .enable("false")) multiplexer_3 (
    .in0(bit_extender_1_out), .in1(salMem), .in2(salRC), .out(multiplexer_3_out), .sel(mux2));  // open: in3
  BR32 br32_1 (
    .RA(multiplexer_2_out), .RW(IR_q[4:0]), .RB(IR_q[9:5]), .busA(br32_1_busa), .busB(br32_1_busb),
    .regW(regW), .busW(multiplexer_3_out), .clk(clk), .clear(clear));
  // Probe on multiplexer_3_out
  ROM #(.addrWidth(7), .dataWidth(4)) rom_2 (.addr({register_2_q, ent}), .data(rom_2_data));  // open: sel
  ROM #(.addrWidth(4), .dataWidth(12)) rom_3 (
    .addr(register_2_q), .data({muxPC, IRwr, mux, mux2, regW, RA, RB, RC, RAMread, memWr, pc}));  // open: sel
  // Probe on br32_1_busa
  Register #(.width(32)) u_RA (.D(br32_1_busa), .en(RA), .Q(salRA), .clk(clk), .clr(clear));
  Register #(.width(32)) u_RB (.D(br32_1_busb), .en(RB), .Q(salRB), .clk(clk), .clr(clear));
  // Probe on br32_1_busb
  Comparator #(.width(32)) comparator_1 (.a(salRA), .b(salRB), .eq(comp));  // open: gt, lt
  Register #(.width(32)) u_RC (.D(adder_2_out), .en(RC), .Q(salRC), .clk(clk), .clr(clear));
  Adder #(.width(32)) adder_2 (.a(salRA), .b(salRB), .out(adder_2_out));  // open: cin, cout
  // Probe on adder_2_out
  // Probe on salRB
  not not_1 (not_1_out, RAMread);
  RAM #(.addrWidth(16), .dataWidth(32), .bus("separate")) ram_1 (
    .addr(salRB[15:0]), .din(salRA), .data({ram_1_data, entrada}), .str(not_1_out), .clk(clk), .ld(RAMread),
    .clr(clear));  // open: sel
  Register #(.width(32)) register_3 (.D({ram_1_data, entrada}), .en(memWr), .Q(salMem), .clk(clk), .clr(clear));

  // Notes on the sheet:
  //   contents of rom_1 (hex, n*v repeats v):
  //   2004 5 1e001 c002 3 20000481 40000020 20001405 20001063 80016062 8000a000 32006 0 60000005 34002
  //   800280a6 20000481 40000023 80032022 80020000 30001 20000481 40000023 80032022 8002a000 80032000
  //   Unidad de Control
  //   contents of rom_2 (hex, n*v repeats v):
  //   8*1 2 3 6 9 b 11*0 8*4 8*5 8*0 8*7 8*8 8*0 8*a 8*0 8*c
  //   contents of rom_3 (hex, n*v repeats v):
  //   404 34 45 34 c 145 14 6 2c5 34 1 234 805
endmodule
