// Logisim project 737215-seg.circ as structural Verilog: 3 circuits, main circuit PROC1
module BR4 (
  input  [1:0] RA,
  input  [1:0] RB,
  input  [1:0] RW,
  input  regW,
  input  clear,
  input  clk,
  input  [31:0] busW,
  output [31:0] busA,
  output [31:0] busB
);

  wire decod1, decod2, decod3, decod4;
  wire [31:0] sal1, sal2, sal3, sal4;

  Decoder #(.select(2), .disabled(0)) decoder_1 (
    .out0(decod1), .out1(decod2), .out2(decod3), .out3(decod4), .sel(RW), .en(regW));
  Register #(.width(32)) register_1 (.D(busW), .en(decod1), .Q(sal1), .clk(clk), .clr(clear));
  Register #(.width(32)) register_2 (.D(busW), .en(decod2), .Q(sal2), .clk(clk), .clr(clear));
  Register #(.width(32)) register_3 (.D(busW), .en(decod3), .Q(sal3), .clk(clk), .clr(clear));
  Register #(.width(32)) register_4 (.D(busW), .en(decod4), .Q(sal4), .clk(clk), .clr(clear));
  Multiplexer #(.select(2), .width(32)) multiplexer_1 (
    .in0(sal1), .in1(sal2), .in2(sal3), .in3(sal4), .out(busA), .sel(RA));  // open: en
  Multiplexer #(.select(2), .width(32)) multiplexer_2 (
    .in0(sal1), .in1(sal2), .in2(sal3), .in3(sal4), .out(busB), .sel(RB));  // open: en
endmodule

module BR32 (
  input  [4:0] RA,
  input  [4:0] RB,
  input  [4:0] RW,
  input  [31:0] busW,
  input  regW,
  input  clk,
  input  clear,
  output [31:0] busA,
  output [31:0] busB
);

  wire Decod1, Decod2, Decod3, Decod4, Decod5, Decod6, Decod7, Decod8;
  wire [31:0] busA1, busA2, busA3, busA4, busA5, busA6, busA7, busA8, busB1, busB2, busB3, busB4, busB5,
       busB6, busB7, busB8;

  Decoder #(.select(3), .disabled(0)) decoder_1 (
    .out0(Decod1), .out1(Decod2), .out2(Decod3), .out3(Decod4), .out4(Decod5), .out5(Decod6), .out6(Decod7),
    .out7(Decod8), .sel(RW[2:0]), .en(regW));
  BR4 br4_1 (
    .regW(Decod1), .RW(RW[4:3]), .busW(busW), .busA(busA1), .busB(busB1), .clear(clear), .clk(clk),
    .RA(RA[4:3]), .RB(RB[4:3]));
  BR4 br4_2 (
    .regW(Decod2), .RW(RW[4:3]), .busW(busW), .busA(busA2), .busB(busB2), .clear(clear), .clk(clk),
    .RA(RA[4:3]), .RB(RB[4:3]));
  BR4 br4_3 (
    .regW(Decod3), .RW(RW[4:3]), .busW(busW), .busA(busA3), .busB(busB3), .clear(clear), .clk(clk),
    .RA(RA[4:3]), .RB(RB[4:3]));
  BR4 br4_4 (
    .regW(Decod4), .RW(RW[4:3]), .busW(busW), .busA(busA4), .busB(busB4), .clear(clear), .clk(clk),
    .RA(RA[4:3]), .RB(RB[4:3]));
  BR4 br4_5 (
    .regW(Decod5), .RW(RW[4:3]), .busW(busW), .busA(busA5), .busB(busB5), .clear(clear), .clk(clk),
    .RA(RA[4:3]), .RB(RB[4:3]));
  BR4 br4_6 (
    .regW(Decod6), .RW(RW[4:3]), .busW(busW), .busA(busA6), .busB(busB6), .clear(clear), .clk(clk),
    .RA(RA[4:3]), .RB(RB[4:3]));
  BR4 br4_7 (
    .regW(Decod7), .RW(RW[4:3]), .busW(busW), .busA(busA7), .busB(busB7), .clear(clear), .clk(clk),
    .RA(RA[4:3]), .RB(RB[4:3]));
  BR4 br4_8 (
    .regW(Decod8), .RW(RW[4:3]), .busW(busW), .busA(busA8), .busB(busB8), .clear(clear), .clk(clk),
    .RA(RA[4:3]), .RB(RB[4:3]));
  Multiplexer #(.select(3), .width(32), .disabled(0)) multiplexer_1 (
    .in0(busA1), .in1(busA2), .in2(busA3), .in3(busA4), .in4(busA5), .in5(busA6), .in6(busA7), .in7(busA8),
    .out(busA), .sel(RA[2:0]));  // open: en
  Multiplexer #(.select(3), .width(32), .disabled(0)) multiplexer_2 (
    .in0(busB1), .in1(busB2), .in2(busB3), .in3(busB4), .in4(busB5), .in5(busB6), .in6(busB7), .in7(busB8),
    .out(busB), .sel(RB[2:0]));  // open: en

  // Other names for the same wires on the sheet: RAmux[2:0] = RA[2:0]; RAent[1:0] = RA[4:3]; RBmux[2:0] = RB[2:0];
  //   RBent[1:0] = RB[4:3]; RWdecod[2:0] = RW[2:0]; RWent[1:0] = RW[4:3]
endmodule

module PROC1 (
);

  wire and_1_out, BEQ, clear, clk, mux, not_1_out, RamRead, regW, Salto, tty_ctrl_1_clk2, tty_ctrl_1_clr,
       tty_ctrl_1_out, tty_OUT;
  wire [1:0] mux2;
  wire [2:0] codOp_ID, VectorDatos_MEM;
  wire [4:0] multiplexer_2_out, RegDstEX, RegDstID, RegDstMEM, RegDstWB, VectorDatos, VectorDatos_EX;
  wire [6:0] entrada, tty_ctrl_1_dout;
  wire [15:0] adder_1_out, multiplexer_1_out, PC_q;
  wire [28:5] IR_q;
  wire [31:0] ALU_EX, ALU_MEM, ALU_WB, br32_1_busa, br32_1_busb, Constante, direccion, direccion_EX,
       direccion_MEM, Mem_WB, multiplexer_3_out, RegA_MEM, RegB_MEM, rom_1_data, salRA, salRB;
  wire [31:7] ram_1_data;

  // Probe on direccion
  Adder #(.width(16)) adder_1 (.a(PC_q), .b(16'h1), .out(adder_1_out));  // open: cin, cout
  Multiplexer #(.width(16), .enable("false")) multiplexer_1 (
    .in0(adder_1_out), .in1(direccion[15:0]), .out(multiplexer_1_out), .sel(and_1_out));
  and and_1 (and_1_out, Salto, BEQ);
  Register #(.width(16), .trigger("falling")) PC (.D(multiplexer_1_out), .en(1'b1), .Q(PC_q), .clk(clk), .clr(clear));
  tty_ctrl tty_ctrl_1 (
    .A({16{1'b1}}), .E(tty_OUT), .out(tty_ctrl_1_out), .clr(tty_ctrl_1_clr), .D(entrada), .clk(clk),
    .Dout(tty_ctrl_1_dout), .clk2(tty_ctrl_1_clk2));
  TTY tty_1 (.data(tty_ctrl_1_dout), .clk(tty_ctrl_1_clk2), .we(tty_ctrl_1_out), .clr(tty_ctrl_1_clr));
  ROM #(.addrWidth(16), .dataWidth(32)) rom_1 (.addr(PC_q), .data(rom_1_data));  // open: sel
  // Probe on codOp_ID
  Register #(.width(32)) IR (.D(rom_1_data), .en(1'b1), .Q({codOp_ID, IR_q, RegDstID}), .clk(clk), .clr(clear));
  ROM #(.addrWidth(3), .dataWidth(7)) rom_2 (.addr(codOp_ID), .data({BEQ, VectorDatos, mux}));  // open: sel
  Clock clock_1 (.out(clk));
  Button button_1 (.out(clear));
  // Probe on IR_q[14:10]
  // Probe on IR_q[9:5]
  // Probe on RegDstID
  assign direccion = {{16{1'b0}}, IR_q[28:13]};  // Bit_Extender bit_extender_1
  Multiplexer #(.width(5), .enable("false")) multiplexer_2 (
    .in0(IR_q[14:10]), .in1(RegDstID), .out(multiplexer_2_out), .sel(mux));
  Multiplexer #(.select(2), .width(32), .enable("false")) multiplexer_3 (
    .in0(Constante), .in1(ALU_WB), .in2(Mem_WB), .out(multiplexer_3_out), .sel(mux2));  // open: in3
  // Probe on mux2
  // Probe on RegDstWB
  // Probe on multiplexer_3_out
  // Probe on br32_1_busa
  BR32 br32_1 (
    .RA(multiplexer_2_out), .RW(RegDstWB), .RB(IR_q[9:5]), .busA(br32_1_busa), .busB(br32_1_busb),
    .regW(regW), .busW(multiplexer_3_out), .clk(clk), .clear(clear));
  // Probe on br32_1_busb
  Register #(.width(5)) register_1 (.D(VectorDatos), .en(1'b1), .Q(VectorDatos_EX), .clk(clk), .clr(clear));
  Register #(.width(5)) register_2 (.D(RegDstID), .en(1'b1), .Q(RegDstEX), .clk(clk), .clr(clear));
  Register #(.width(32)) RA (.D(br32_1_busa), .en(1'b1), .Q(salRA), .clk(clk), .clr(clear));
  Comparator #(.width(32)) comparator_1 (.a(br32_1_busa), .b(br32_1_busb), .eq(Salto));  // open: gt, lt
  Register #(.width(32)) RB (.D(br32_1_busb), .en(1'b1), .Q(salRB), .clk(clk), .clr(clear));
  Register #(.width(32)) register_3 (.D(direccion), .en(1'b1), .Q(direccion_EX), .clk(clk), .clr(clear));
  Adder #(.width(32)) adder_2 (.a(salRA), .b(salRB), .out(ALU_EX));  // open: cin, cout
  // Probe on ALU_EX
  Register #(.width(5)) register_4 (
    .D(VectorDatos_EX), .en(1'b1), .Q({RamRead, tty_OUT, VectorDatos_MEM}), .clk(clk), .clr(clear));
  Register #(.width(5)) register_5 (.D(RegDstEX), .en(1'b1), .Q(RegDstMEM), .clk(clk), .clr(clear));
  Register #(.width(32)) register_6 (.D(salRB), .en(1'b1), .Q(RegB_MEM), .clk(clk), .clr(clear));
  Register #(.width(32)) register_7 (.D(direccion_EX), .en(1'b1), .Q(direccion_MEM), .clk(clk), .clr(clear));
  Register #(.width(32)) register_8 (.D(ALU_EX), .en(1'b1), .Q(ALU_MEM), .clk(clk), .clr(clear));
  Register #(.width(32)) register_9 (.D(salRA), .en(1'b1), .Q(RegA_MEM), .clk(clk), .clr(clear));
  not not_1 (not_1_out, RamRead);
  RAM #(.addrWidth(16), .dataWidth(32), .bus("separate")) ram_1 (
    .addr(RegB_MEM[15:0]), .din(RegA_MEM), .data({ram_1_data, entrada}), .str(RamRead), .clk(clk),
    .ld(not_1_out), .clr(clear));  // open: sel
  // Probe on VectorDatos_MEM
  Register #(.width(3)) register_10 (.D(VectorDatos_MEM), .en(1'b1), .Q({mux2, regW}), .clk(clk), .clr(clear));
  Register #(.width(32)) register_11 (.D(ALU_MEM), .en(1'b1), .Q(ALU_WB), .clk(clk), .clr(clear));
  Register #(.width(32)) register_12 (.D({ram_1_data, entrada}), .en(tty_OUT), .Q(Mem_WB), .clk(clk), .clr(clear));
  Register #(.width(5)) register_13 (.D(RegDstMEM), .en(1'b1), .Q(RegDstWB), .clk(clk), .clr(clear));
  Register #(.width(32)) register_14 (.D(direccion_MEM), .en(1'b1), .Q(Constante), .clk(clk), .clr(clear));

  // Notes on the sheet:
  //   ETAPA IF
  //   contents of rom_1 (hex, n*v repeats v):
  //   2004 5 1e001 c002 3 a0000000 20000481 a0000000 a0000000 a0000000 40000020 a0000000 a0000000 a0000000
  //   20001405 20000c83 a0000000 a0000000 a0000000 8002a062 8000c000 32006 0 a0000000 a0000000 a0000000
  //   60000005 34002 800480a6 20000481 a0000000 a0000000 a0000000 40000023 8005e022 8003a000 30001
  //   a0000000 a0000000 a0000000 20000481 a0000000 a0000000 a0000000 40000023 8005e022 80050000 8005e000
  //   contents of rom_2 (hex, n*v repeats v):
  //   3 6 1a 20 41
  //   ETAPA ID
  //   ETAPA EX
  //   ETAPA MEM
  //   ETAPA WB
endmodule
