// Logisim project 737215-cache.circ as structural Verilog: 1 circuit, main circuit 737215-cache
module _737215_cache (
);

  wire and_2_out, bloque1, bloque2, clear, clk, comparator_1_eq, DIR, DIRNeg, HIT, mem_en, or_1_out, regA,
       regB, regC, regD, WAY, write, writeRam1, writeRam2;
  wire [3:0] counter_1_q;
  wire [6:0] ETIQUETA;
  wire [7:0] adder_1_out, register_1_q, salRAM1, salRAM2;
  wire [8:0] salROM;
  wire [31:0] bus, datoA, datoB, datoC, datoD, ent1, ent2, ent3, ent4, ent5, ent6, ent7, ent8,
       multiplexer_3_out, samMUXA, samMUXB;

  not not_1 (mem_en, HIT);
  Comparator comparator_1 (.a({1'b1, ETIQUETA}), .b(salRAM1), .eq(comparator_1_eq));  // open: gt, lt
  Comparator comparator_2 (.a({1'b1, ETIQUETA}), .b(salRAM2), .eq(WAY));  // open: gt, lt
  Counter #(.width(4), .max('hf)) counter_1 (
    .D(counter_1_q), .Q(counter_1_q), .clk(clk), .clr(or_1_out));  // open: load, count, carry
  RAM #(.addrWidth(5), .bus("separate")) ram_1 (
    .addr(salROM[8:4]), .din({1'b1, ETIQUETA}), .data(salRAM1), .str(writeRam1), .clk(clk), .clr(clear));  // open: sel, ld
  RAM #(.addrWidth(5), .dataWidth(1), .bus("separate")) ram_2 (
    .addr(salROM[8:4]), .din(DIRNeg), .data(DIR), .str(write), .clk(clk), .ld(1'b1), .clr(clear));  // open: sel
  or or_1 (or_1_out, HIT, clear);
  or or_2 (HIT, comparator_1_eq, WAY);
  not not_2 (DIRNeg, DIR);
  Decoder #(.select(4), .enable("false")) decoder_1 (
    .out4(regA), .out6(regB), .out8(regC), .out10(regD), .out11(write), .sel(counter_1_q));  // open: out0, out1, out2, out3, out5, out7, out9, out12, out13, out14, out15
  Clock clock_1 (.out(clk));
  Button button_1 (.out(clear));
  and and_1 (writeRam2, write, DIR);
  and and_2 (and_2_out, write, DIR);
  and and_3 (writeRam1, write, DIRNeg);
  RAM #(.addrWidth(5), .bus("separate")) ram_3 (
    .addr(salROM[8:4]), .din({1'b1, ETIQUETA}), .data(salRAM2), .str(writeRam2), .clk(clk), .clr(clear));  // open: sel, ld
  Decoder #(.enable("false")) decoder_2 (.out0(bloque1), .out1(bloque2), .sel(and_2_out));
  Adder adder_1 (.a(register_1_q), .b(8'h1), .out(adder_1_out));  // open: cin, cout
  Register register_1 (.D(adder_1_out), .en(HIT), .Q(register_1_q), .clk(clk), .clr(clear));
  // MP_main main_1: pin names not known; wires that end beside it: {ETIQUETA, salROM}, mem_en, clk, bus
  Register #(.width(32)) register_2 (.D(bus), .en(regA), .Q(datoA), .clk(clk), .clr(clear));
  Register #(.width(32)) register_3 (.D(bus), .en(regB), .Q(datoB), .clk(clk), .clr(clear));
  Register #(.width(32)) register_4 (.D(bus), .en(regC), .Q(datoC), .clk(clk), .clr(clear));
  Register #(.width(32)) register_5 (.D(bus), .en(regD), .Q(datoD), .clk(clk), .clr(clear));
  ROM #(.dataWidth(16)) rom_1 (.addr(register_1_q), .data({ETIQUETA, salROM}));  // open: sel
  RAM #(.addrWidth(5), .dataWidth(32), .bus("separate")) ram_4 (
    .addr(salROM[8:4]), .din(datoA), .data(ent1), .str(bloque1), .clk(clk), .ld(1'b1), .clr(clear));  // open: sel
  RAM #(.addrWidth(5), .dataWidth(32), .bus("separate")) ram_5 (
    .addr(salROM[8:4]), .din(datoB), .data(ent2), .str(bloque1), .clk(clk), .ld(1'b1), .clr(clear));  // open: sel
  RAM #(.addrWidth(5), .dataWidth(32), .bus("separate")) ram_6 (
    .addr(salROM[8:4]), .din(datoC), .data(ent3), .str(bloque1), .clk(clk), .ld(1'b1), .clr(clear));  // open: sel
  RAM #(.addrWidth(5), .dataWidth(32), .bus("separate")) ram_7 (
    .addr(salROM[8:4]), .din(datoD), .data(ent4), .str(bloque1), .clk(clk), .ld(1'b1), .clr(clear));  // open: sel
  RAM #(.addrWidth(5), .dataWidth(32), .bus("separate")) ram_8 (
    .addr(salROM[8:4]), .din(datoA), .data(ent5), .str(bloque2), .clk(clk), .ld(1'b1), .clr(clear));  // open: sel
  RAM #(.addrWidth(5), .dataWidth(32), .bus("separate")) ram_9 (
    .addr(salROM[8:4]), .din(datoB), .data(ent6), .str(bloque2), .clk(clk), .ld(1'b1), .clr(clear));  // open: sel
  RAM #(.addrWidth(5), .dataWidth(32), .bus("separate")) ram_10 (
    .addr(salROM[8:4]), .din(datoC), .data(ent7), .str(bloque2), .clk(clk), .ld(1'b1), .clr(clear));  // open: sel
  RAM #(.addrWidth(5), .dataWidth(32), .bus("separate")) ram_11 (
    .addr(salROM[8:4]), .din(datoD), .data(ent8), .str(bloque2), .clk(clk), .ld(1'b1), .clr(clear));  // open: sel
  Multiplexer #(.select(2), .width(32), .enable("false")) multiplexer_1 (
    .in0(ent1), .in1(ent2), .in2(ent3), .in3(ent4), .out(samMUXA), .sel(salROM[3:2]));
  Multiplexer #(.select(2), .width(32), .enable("false")) multiplexer_2 (
    .in0(ent5), .in1(ent6), .in2(ent7), .in3(ent8), .out(samMUXB), .sel(salROM[3:2]));
  Multiplexer #(.width(32), .enable("false")) multiplexer_3 (
    .in0(samMUXA), .in1(samMUXB), .out(multiplexer_3_out), .sel(WAY));
  // Probe on multiplexer_3_out

  // Other names for the same wires on the sheet: pc = HIT; word[1:0] = salROM[3:2]; SET[4:0] = salROM[8:4];
  //   salROM[15:9] = ETIQUETA; SEÑAL[6:0] = ETIQUETA

  // Notes on the sheet:
  //   Unidad  de Control
  //   Gestión de etiquetas
  //   Memoria principal
  //   contents of rom_1 (hex, n*v repeats v):
  //   400 c00 1800 c04 290 1290 e90 1294 f804 5204 5604 560c
  //   Gestión de datos
endmodule
